# Fritzing sketch 04- Resistors in parallel (saved by Fritzing 0.9.3b)
breadboards: 1

parts:
  R1 = Resistor [tolerance=±5% resistance=1k package=THT]
  R2 = Resistor [tolerance=±5% resistance=10k package=THT]
  R3 = Resistor [tolerance=±5% resistance=100k package=THT]

nets:
  N1: R1.Pin_0, R2.Pin_0, R3.Pin_0
  N2: R1.Pin_1, R2.Pin_1, R3.Pin_1
