# Fritzing sketch 06- Diode Riverse direction with an LED with 3.3V (saved by Fritzing 0.9.3b)
breadboards: 1

parts:
  YwRobot_Power_Supply1 = YwRobot Breadboard Power Supply [part_number=545043]
  LED2 = smd LED [color="Red (633nm)" package="0603 [SMD]"]
  D1 = Rectifier Diode [part_number=1N4007 package="300 mil [THT]"]  # not connected

nets:
  N1: YwRobot_Power_Supply1.VCC#5, YwRobot_Power_Supply1.VCC#6
  N2: YwRobot_Power_Supply1.VCC#9, YwRobot_Power_Supply1.VCC#10
  N3: YwRobot_Power_Supply1.GND#11, YwRobot_Power_Supply1.GND#12, LED2.cathode
  N4: YwRobot_Power_Supply1.GND#13, YwRobot_Power_Supply1.GND#14

custom parts:
  YwRobot Breadboard Power Supply: The YwRobot Breadboard Power Supply (MB-V2) has two power rails; they can be 5V or 3V3. Power to the module can be provided through the female USB socket or through the A10 (female) 2.1mm power jack.
