# Fritzing sketch 07- 555 Astable multivibrator (saved by Fritzing 0.9.3b)
breadboards: 1

parts:
  U1 = 555 Timer [package="SO8 [SMD]"]  # not connected
  R1 = Resistor [tolerance=±5% resistance=47k package=THT]
  R3 = Resistor [tolerance=±5% resistance=330 package=THT]
  LED1 = LED - 5mm [color="Red (633nm)" package="5 mm [THT]"]
  YwRobot_Power_Supply1 = YwRobot Breadboard Power Supply [part_number=545043]
  R2 = Resistor [tolerance=±5% resistance=47k package=THT]
  C1 = Ceramic Capacitor [capacitance=10nF package="100 mil [THT, multilayer]"]
  C2 = Ceramic Capacitor [capacitance=100nF package="100 mil [THT, multilayer]"]

nets:
  N1: R1.Pin_0, R2.Pin_0
  N2: R1.Pin_1, YwRobot_Power_Supply1.VCC#9, YwRobot_Power_Supply1.VCC#10
  N3: R3.Pin_1, LED1.anode
  N4: LED1.cathode, YwRobot_Power_Supply1.GND#11, YwRobot_Power_Supply1.GND#12, C1.0, C2.1
  N5: YwRobot_Power_Supply1.VCC#5, YwRobot_Power_Supply1.VCC#6
  N6: YwRobot_Power_Supply1.GND#13, YwRobot_Power_Supply1.GND#14
  N7: R2.Pin_1, C1.1

custom parts:
  YwRobot Breadboard Power Supply: The YwRobot Breadboard Power Supply (MB-V2) has two power rails; they can be 5V or 3V3. Power to the module can be provided through the female USB socket or through the A10 (female) 2.1mm power jack.
