# Fritzing sketch 08- Arduino Nano LED Blinking (saved by Fritzing 0.9.3b)
breadboards: 1

parts:
  LED2 = smd LED [color="Red (633nm)" package="0603 [SMD]"]
  Part1 = Arduino Nano (Rev3.0)
  R1 = Resistor [tolerance=±5% resistance=330 package=THT]

nets:
  N1: LED2.cathode, Part1.GND
  N2: LED2.anode, R1.Pin_0
  N3: Part1.D13/SCK, R1.Pin_1
