# Fritzing sketch 09- Arduino Nano LPG Detection (saved by Fritzing 0.9.3b)
breadboards: 1

parts:
  Part1 = Arduino Nano (Rev3.0)
  MQ-2_/_MQ-3 = MQ-3 breakout

nets:
  GND: Part1.GND, MQ-2_/_MQ-3.GND
  5V: Part1.5V, MQ-2_/_MQ-3.VCC
  N1: Part1.A0, MQ-2_/_MQ-3.AO

custom parts:
  MQ-3 breakout: Alcohol sensor is capable of detecting alcohol (ethanol) particles on itself and gives the information in digital form back to us to manipulate with it. SKU:101251 • Voltage: 5V DC • Power: max 750mW • Measurement range: 0.04-4mg/L
