# Fritzing sketch 10- Arduino Nano MPU6050 accelerometer (saved by Fritzing 0.9.3b)
breadboards: 1

parts:
  Part1 = Arduino Nano (Rev3.0)
  MPU6050_Module = InvenSense MPU6050

nets:
  GND: Part1.GND, MPU6050_Module.GND
  5V: Part1.5V, MPU6050_Module.VCC
  N1: Part1.A5, MPU6050_Module.SCL
  N2: Part1.A4, MPU6050_Module.SDA
