# Fritzing sketch 11- Arduino Nano Buzzer simulation (saved by Fritzing 0.9.3b)
breadboards: 1

parts:
  Part1 = Arduino Nano (Rev3.0)
  5V_Buzzer = Piezo Buzzer

nets:
  N1: Part1.GND, 5V_Buzzer.pin_2
  N2: Part1.D8, 5V_Buzzer.pin_1

custom parts:
  Piezo Buzzer: Part from https://www.nutsvolts.com/magazine/article/november2012_SmileysWorkshop modified to be .3 in spacing to match the adafruit buzzer 5V breadboard friendly part.
