# Fritzing sketch 12- Arduino Nano Motor Driving with BD 139 Transistor (saved by Fritzing 0.9.3b)
breadboards: 1

parts:
  Part1 = Arduino Nano (Rev3.0)
  D1 = Rectifier Diode [part_number=1N4001 package="300 mil [THT]"]  # not connected
  R1 = Resistor [tolerance=±5% resistance=1k package=THT]
  YwRobot_Power_Supply1 = YwRobot Breadboard Power Supply [part_number=545043]
  M1 = DC Motor
  Q1 = NPN-Transistor [part_number=BD139 package="TO92 [THT]"]

nets:
  N1: Part1.GND, YwRobot_Power_Supply1.GND#13, YwRobot_Power_Supply1.GND#14, Q1.E
  N2: Part1.D4, R1.Pin_0
  N3: R1.Pin_1, Q1.B
  N4: YwRobot_Power_Supply1.VCC#5, YwRobot_Power_Supply1.VCC#6
  N5: YwRobot_Power_Supply1.VCC#9, YwRobot_Power_Supply1.VCC#10, M1.pin_2
  N6: YwRobot_Power_Supply1.GND#11, YwRobot_Power_Supply1.GND#12
  N7: M1.pin_1, Q1.C

custom parts:
  YwRobot Breadboard Power Supply: The YwRobot Breadboard Power Supply (MB-V2) has two power rails; they can be 5V or 3V3. Power to the module can be provided through the female USB socket or through the A10 (female) 2.1mm power jack.
