# Fritzing sketch 13- Transistor Driver Circuit Using BC547 (saved by Fritzing 0.9.3b)
breadboards: 1

parts:
  Part1 = Arduino Nano (Rev3.0)
  R1 = Resistor [tolerance=±5% resistance=1k package=THT]
  D1 = Rectifier Diode [part_number=1N4007 package="300 mil [THT]"]  # not connected
  5V_Relay = songle relay
  Q1 = NPN-Transistor [part_number=BC547 package="TO92 [THT]"]

nets:
  N1: Part1.GND, Q1.E
  N2: Part1.D4, R1.Pin_0
  5V: Part1.5V, 5V_Relay.VCC
  N3: R1.Pin_1, Q1.B
  N4: 5V_Relay.GND, Q1.C
