# Fritzing sketch 14- Reed switch and Buzzer simulation with Arduino Nano (saved by Fritzing 0.9.3b)
breadboards: 1

parts:
  Part1 = Arduino Nano (Rev3.0)
  R1 = Resistor [tolerance=±5% resistance=10k package=THT]
  Reed_Switch = SWITCH-MOMENTARY-2 [package=reed_switch_plastic]
  5V_Buzzer = Piezo Buzzer

nets:
  N1: Part1.GND, R1.Pin_0, Reed_Switch.1, 5V_Buzzer.pin_2
  N2: Part1.D2, Reed_Switch.2
  N3: Part1.D5, 5V_Buzzer.pin_1
  N4: Part1.5V, R1.Pin_1

custom parts:
  Piezo Buzzer: Part from https://www.nutsvolts.com/magazine/article/november2012_SmileysWorkshop modified to be .3 in spacing to match the adafruit buzzer 5V breadboard friendly part.
