# Fritzing sketch 14- Reed switch and Buzzer simulation (saved by Fritzing 0.9.3b)
breadboards: 1

parts:
  Reed_Switch = SWITCH-MOMENTARY-2 [package=reed_switch_plastic]
  Q1 = NPN-Transistor [part_number=BC547 package="TO92 [THT]"]
  YwRobot_Power_Supply1 = YwRobot Breadboard Power Supply [part_number=545043]
  R1 = Resistor [tolerance=±5% resistance=1k package=THT]
  5V_Buzzer = Piezo Buzzer

nets:
  N1: Reed_Switch.1, R1.Pin_1
  N2: Reed_Switch.2, Q1.B
  N3: Q1.E, 5V_Buzzer.pin_1
  N4: Q1.C, YwRobot_Power_Supply1.GND#13, YwRobot_Power_Supply1.GND#14
  N5: YwRobot_Power_Supply1.VCC#5, YwRobot_Power_Supply1.VCC#6
  N6: YwRobot_Power_Supply1.VCC#9, YwRobot_Power_Supply1.VCC#10, R1.Pin_0, 5V_Buzzer.pin_2
  N7: YwRobot_Power_Supply1.GND#11, YwRobot_Power_Supply1.GND#12

custom parts:
  YwRobot Breadboard Power Supply: The YwRobot Breadboard Power Supply (MB-V2) has two power rails; they can be 5V or 3V3. Power to the module can be provided through the female USB socket or through the A10 (female) 2.1mm power jack.
  Piezo Buzzer: Part from https://www.nutsvolts.com/magazine/article/november2012_SmileysWorkshop modified to be .3 in spacing to match the adafruit buzzer 5V breadboard friendly part.
