# Fritzing sketch 15- PIR Sensor interfacing with Arduino Nano (saved by Fritzing 0.9.3b)
breadboards: 1

parts:
  Part1 = Arduino Nano (Rev3.0)
  LED1 = LED - 5mm [color="Red (633nm)" package="5 mm [THT]"]
  R1 = Resistor [tolerance=±5% resistance=330 package=THT]
  PIR1 = PIR sensor

nets:
  N1: Part1.GND, LED1.cathode
  N2: Part1.D2, PIR1.SIG
  N3: Part1.D12/MISO, R1.Pin_0
  N4: LED1.anode, R1.Pin_1
