# Fritzing sketch 16- Ultrasonic sensor interfacing with Arduino Nano (saved by Fritzing 0.9.3b)
breadboards: 1

parts:
  Part1 = Arduino Nano (Rev3.0)
  Ultrasonic_Sensor = SRF05 Ultrasonic Rangefinder

nets:
  GND: Part1.GND, Ultrasonic_Sensor.GND
  N1: Part1.D11/MOSI, Ultrasonic_Sensor.Trig
  N2: Part1.D12/MISO, Ultrasonic_Sensor.Echo
  5V: Part1.5V, Ultrasonic_Sensor.VCC
