# Fritzing sketch 18- DHT 11 interfacing with Arduino Nano serial and LCD (saved by Fritzing 0.9.3b)
breadboards: 1

parts:
  Part1 = Arduino Nano (Rev3.0)
  LCD1 = LCD screen
  U1 = POT [package=pot_mammoth]
  DHT11_1 = DHT11 module

nets:
  GND: Part1.GND, LCD1.VSS, LCD1.R/W, U1.S, DHT11_1.GND
  N1: Part1.D2, LCD1.RS
  N2: Part1.D3, LCD1.E
  N3: Part1.D4, LCD1.DB4
  N4: Part1.D5, LCD1.DB5
  N5: Part1.D6, LCD1.DB6
  N6: Part1.D7, LCD1.DB7
  N7: Part1.D12/MISO, DHT11_1.DATA
  5V: Part1.5V, LCD1.VDD, LCD1.LED+, U1.E, DHT11_1.VCC
  N8: LCD1.V0, U1.A

custom parts:
  DHT11 module: DHT11 black pcb module
