# Fritzing sketch 19- Wifi Module interfacing with Arduino Nano (saved by Fritzing 0.9.3b)
breadboards: 1

parts:
  Part1 = Arduino Nano (Rev3.0)
  U1 = ESP8266 WiFi Module [part_number=ESP8266]

nets:
  GND: Part1.GND, U1.GND
  N1: Part1.D2, U1.RXD
  N2: Part1.D3, U1.TXD
  3V3: Part1.3V3, U1.VCC, U1.CH_PD

custom parts:
  ESP8266 WiFi Module: Generic WiFi Module based on the ESP8266 with onboard PCB antenna and UART communications
