# Fritzing sketch 22- Keypad 4X4 interfacing with Arduino Nano (saved by Fritzing 0.9.3b)
breadboards: 1

parts:
  Part1 = Arduino Nano (Rev3.0)
  Part3 = 4x4 Keypad [part_number=101207]

nets:
  N1: Part1.D2, Part3.8
  N2: Part1.D3, Part3.7
  N3: Part1.D4, Part3.6
  N4: Part1.D5, Part3.5
  N5: Part1.D6, Part3.4
  N6: Part1.D7, Part3.3
  N7: Part1.D8, Part3.2
  N8: Part1.D9, Part3.1

custom parts:
  4x4 Keypad: Matrix membrane keypad 4x4
