# Fritzing sketch 23- Servo Motor Interfacing with Arduino Nano (saved by Fritzing 0.9.3b)
breadboards: 1

parts:
  Part1 = Arduino Nano (Rev3.0)
  J1 = Basic Servo

nets:
  GND: Part1.GND, J1.gnd
  N1: Part1.D9, J1.pulse
  5V: Part1.5V, J1.vcc
